# Fritzing sketch board (saved by Fritzing 0.9.3b)

parts:
  WeMos_D1_Mini1 = WeMos D1 Mini
  Grove1 = Grove OLED 128x96

nets:
  5V: WeMos_D1_Mini1.5V, Grove1.VCC
  N1: WeMos_D1_Mini1.D1, Grove1.SCL
  N2: WeMos_D1_Mini1.D2, Grove1.SDA
  N3: WeMos_D1_Mini1.G, Grove1.GND
